// Logisim project 3bit_comparator_using_1bit_comparator.circ as structural Verilog: 1 circuit, main circuit main
module main (
  input  A1,
  input  B1,
  input  A0,
  input  B0,
  input  A2,
  input  B2
);

  wire E0_out, E1_out, E2_out, G0_out, G1_out, L0_out, L1_out, nand_1_out, nand_2_out, nand_3_out,
       nand_4_out, nand_5_out, nand_6_out, nand_7_out, nand_8_out, nand_9_out, nand_10_out, nand_11_out,
       nand_12_out, nand_13_out, nand_14_out, nand_15_out, nand_16_out, nand_17_out, nand_18_out,
       nand_19_out, nand_20_out, nand_21_out, nand_22_out, nand_23_out, nand_24_out, nand_25_out,
       nand_26_out, nand_27_out, nand_28_out, nand_29_out, nand_30_out, nand_31_out, nand_32_out;

  nand nand_1 (nand_1_out, A2, A2);
  nand nand_2 (nand_2_out, B2, B2);
  nand nand_3 (nand_3_out, A1, A1);
  nand nand_4 (nand_4_out, B1, B1);
  nand nand_5 (nand_5_out, A0, A0);
  nand nand_6 (nand_6_out, B0, B0);
  nand nand_7 (nand_7_out, B1, nand_3_out);
  nand nand_8 (nand_8_out, nand_4_out, nand_3_out);
  nand nand_9 (nand_9_out, B1, A1);
  nand nand_10 (nand_10_out, nand_4_out, A1);
  nand nand_11 (nand_11_out, B0, nand_5_out);
  nand nand_12 (nand_12_out, nand_6_out, nand_5_out);
  nand nand_13 (nand_13_out, B0, A0);
  nand nand_14 (nand_14_out, nand_6_out, A0);
  nand nand_15 (nand_15_out, B2, nand_1_out);
  nand nand_16 (nand_16_out, nand_2_out, nand_1_out);
  nand nand_17 (nand_17_out, B2, A2);
  nand nand_18 (nand_18_out, nand_2_out, A2);
  // NAND_Gate L2 has open pins: in0=nand_15_out, in1=nand_15_out, out=open
  nand E2 (E2_out, nand_16_out, nand_17_out);
  // NAND_Gate G2 has open pins: in0=nand_18_out, in1=nand_18_out, out=open
  nand L1 (L1_out, nand_7_out, nand_7_out);
  nand E1 (E1_out, nand_8_out, nand_9_out);
  nand G1 (G1_out, nand_10_out, nand_10_out);
  nand L0 (L0_out, nand_11_out, nand_11_out);
  nand E0 (E0_out, nand_12_out, nand_13_out);
  nand G0 (G0_out, nand_14_out, nand_14_out);
  nand nand_19 (nand_19_out, E2_out, L1_out);
  nand nand_20 (nand_20_out, E2_out, E1_out);
  nand nand_21 (nand_21_out, E2_out, G1_out);
  nand nand_22 (nand_22_out, nand_20_out, nand_20_out);
  nand nand_23 (nand_23_out, nand_22_out, L0_out);
  nand nand_24 (nand_24_out, nand_22_out, E0_out);
  nand nand_25 (nand_25_out, nand_22_out, G0_out);
  nand nand_26 (nand_26_out, nand_19_out, nand_23_out);
  nand nand_27 (nand_27_out, nand_24_out, nand_24_out);
  nand nand_28 (nand_28_out, nand_21_out, nand_25_out);
  nand nand_29 (nand_29_out, nand_28_out, nand_28_out);
  nand nand_30 (nand_30_out, nand_26_out, nand_26_out);
  nand nand_31 (nand_31_out, nand_15_out, nand_30_out);
  nand nand_32 (nand_32_out, nand_18_out, nand_29_out);
  LED L (.in(nand_31_out));
  LED E (.in(nand_27_out));
  LED G (.in(nand_32_out));
endmodule
