// Logisim project 3bit_fullsubtractor.circ as structural Verilog: 1 circuit, main circuit main
module main (
  input  GND,
  input  A0,
  input  A1,
  input  A2,
  input  B0,
  input  B1,
  input  B2
);

  wire nand_1_out, nand_2_out, nand_3_out, nand_4_out, nand_5_out, nand_6_out, nand_7_out, nand_8_out,
       nand_9_out, nand_10_out, nand_11_out, nand_12_out, nand_13_out, nand_14_out, nand_15_out, nand_16_out,
       nand_17_out, nand_18_out, nand_19_out, nand_20_out, nand_21_out, nand_22_out, nand_23_out,
       nand_24_out, nand_25_out, nand_26_out, nand_27_out;

  nand nand_1 (nand_1_out, GND, B0);
  nand nand_2 (nand_2_out, nand_23_out, B1);
  nand nand_3 (nand_3_out, nand_25_out, B2);
  nand nand_4 (nand_4_out, GND, nand_1_out);
  nand nand_5 (nand_5_out, nand_1_out, B0);
  nand nand_6 (nand_6_out, nand_23_out, nand_2_out);
  nand nand_7 (nand_7_out, nand_2_out, B1);
  nand nand_8 (nand_8_out, nand_25_out, nand_3_out);
  nand nand_9 (nand_9_out, nand_3_out, B2);
  nand nand_10 (nand_10_out, nand_4_out, nand_5_out);
  nand nand_11 (nand_11_out, nand_6_out, nand_7_out);
  nand nand_12 (nand_12_out, nand_8_out, nand_9_out);
  nand nand_13 (nand_13_out, nand_10_out, A0);
  nand nand_14 (nand_14_out, nand_11_out, A1);
  nand nand_15 (nand_15_out, nand_12_out, A2);
  nand nand_16 (nand_16_out, nand_10_out, nand_13_out);
  nand nand_17 (nand_17_out, nand_13_out, A0);
  nand nand_18 (nand_18_out, nand_11_out, nand_14_out);
  nand nand_19 (nand_19_out, nand_14_out, A1);
  nand nand_20 (nand_20_out, nand_12_out, nand_15_out);
  nand nand_21 (nand_21_out, nand_15_out, A2);
  nand nand_22 (nand_22_out, nand_16_out, nand_17_out);
  nand nand_23 (nand_23_out, nand_16_out, nand_1_out);
  nand nand_24 (nand_24_out, nand_18_out, nand_19_out);
  nand nand_25 (nand_25_out, nand_18_out, nand_2_out);
  nand nand_26 (nand_26_out, nand_20_out, nand_21_out);
  nand nand_27 (nand_27_out, nand_20_out, nand_3_out);
  LED D0 (.in(nand_22_out));
  LED D1 (.in(nand_24_out));
  LED D2 (.in(nand_26_out));
  LED Bo (.in(nand_27_out));

  // Notes on the sheet:
  //   Difference Output
  //   Difference Output
  //   Difference Output
  //   Borrow Output
endmodule
