// Logisim project up_counter - Copy.circ as structural Verilog: 1 circuit, main circuit main
module main (
);

  wire clock_1_out, nand_1_out, nand_2_out, nand_3_out, nand_4_out, nand_5_out, nand_6_out, nand_7_out,
       nand_8_out, nand_9_out, t_ff_1_q, t_ff_2_q, t_ff_3_q, t_ff_4_q;

  Clock clock_1 (.out(clock_1_out));
  LED A (.in(t_ff_1_q));
  T_Flip_Flop t_ff_1 (.T(nand_2_out), .clk(clock_1_out), .Q(t_ff_1_q), .reset(nand_9_out), .preset(1'b1));  // open: Qn
  nand nand_1 (nand_1_out, t_ff_1_q, nand_2_out);
  T_Flip_Flop t_ff_2 (.T(nand_1_out), .clk(clock_1_out), .Q(t_ff_2_q), .reset(nand_9_out), .preset(1'b1));  // open: Qn
  nand nand_2 (nand_2_out, t_ff_2_q, t_ff_4_q);
  LED B (.in(t_ff_2_q));
  nand nand_3 (nand_3_out, t_ff_1_q, t_ff_2_q);
  T_Flip_Flop t_ff_3 (.T(nand_4_out), .clk(clock_1_out), .Q(t_ff_3_q), .reset(nand_9_out), .preset(1'b1));  // open: Qn
  LED C (.in(t_ff_3_q));
  nand nand_4 (nand_4_out, nand_3_out, nand_3_out);
  nand nand_5 (nand_5_out, t_ff_3_q, nand_4_out);
  T_Flip_Flop t_ff_4 (.T(nand_6_out), .clk(clock_1_out), .Q(t_ff_4_q), .reset(nand_9_out), .preset(1'b1));  // open: Qn
  LED D (.in(t_ff_4_q));
  nand nand_6 (nand_6_out, nand_5_out, nand_2_out);
  nand nand_7 (nand_7_out, t_ff_1_q, t_ff_2_q);
  nand nand_8 (nand_8_out, nand_7_out, nand_7_out);
  nand nand_9 (nand_9_out, nand_8_out, t_ff_4_q);
endmodule
