// Logisim project 4bit_ripple_up_down.circ as structural Verilog: 1 circuit, main circuit main
module main (
  input  M,
  input  in_2
);

  wire clock_1_out, nand_2_out, nand_3_out, nand_4_out, nand_5_out, nand_6_out, nand_7_out, nand_8_out,
       nand_9_out, nand_10_out, t_ff_1_q, t_ff_1_qn, t_ff_2_q, t_ff_2_qn, t_ff_3_q, t_ff_3_qn;

  Clock clock_1 (.out(clock_1_out));
  LED A (.in(t_ff_1_q));
  nand nand_1 (M, M, M);
  T_Flip_Flop t_ff_1 (.T(in_2), .clk(clock_1_out), .Q(t_ff_1_q), .Qn(t_ff_1_qn));  // open: reset, preset
  nand nand_2 (nand_2_out, M, t_ff_1_q);
  nand nand_3 (nand_3_out, M, t_ff_1_qn);
  T_Flip_Flop t_ff_2 (.T(in_2), .clk(nand_4_out), .Q(t_ff_2_q), .Qn(t_ff_2_qn));  // open: reset, preset
  nand nand_4 (nand_4_out, nand_2_out, nand_3_out);
  LED B (.in(t_ff_2_q));
  nand nand_5 (nand_5_out, M, t_ff_2_q);
  nand nand_6 (nand_6_out, M, t_ff_2_qn);
  T_Flip_Flop t_ff_3 (.T(in_2), .clk(nand_7_out), .Q(t_ff_3_q), .Qn(t_ff_3_qn));  // open: reset, preset
  nand nand_7 (nand_7_out, nand_5_out, nand_6_out);
  LED C (.in(t_ff_3_q));
  nand nand_8 (nand_8_out, M, t_ff_3_q);
  nand nand_9 (nand_9_out, nand_8_out, nand_10_out);
  nand nand_10 (nand_10_out, M, t_ff_3_qn);
  T_Flip_Flop t_ff_4 (.T(in_2), .clk(nand_9_out), .Q(M));  // open: Qn, reset, preset
  LED D (.in(M));
endmodule
